// Logisim project 单周期CPU.circ as structural Verilog: 11 circuits, main circuit main
module main (
  input  reset,
  output [31:0] Instr,
  output [31:0] pc,
  output out_4,
  output [4:0] out_5,
  output [31:0] RegDaata,
  output out_7,
  output [31:0] out_8,
  output [31:0] out_9
);

  wire clk, controller_1_ctrl, controller_1_grf_op1;
  wire [1:0] controller_1_alu_op, controller_1_grf_op2, controller_1_op;
  wire [4:0] \指令解读_1_rd , \指令解读_1_rs_base , \指令解读_1_rt ;
  wire [15:0] im_of;
  wire [31:0] bit_extender_1_out, bit_extender_2_out, dm_1_memdata_2, grf_1_rd1, multiplexer_3_out;

  Clock clock_1 (.out(clk));
  IFU ifu_1 (.ctrl_addr(im_of), .clk(clk), .rst(reset), .ctrl(controller_1_ctrl), .PC(pc), .Instr(Instr));
  Controller controller_1 (
    .Instr(Instr), .ALUout(out_8), .ctrl(controller_1_ctrl), .WE(out_4), .GRF_op1(controller_1_grf_op1),
    .GRF_op2(controller_1_grf_op2), .op(controller_1_op), .ALU_op(controller_1_alu_op), .MemWrite(out_7));
  \指令解读  \u_指令解读_1  (
    .Instr(Instr), .im_of(im_of), .rd(\指令解读_1_rd ), .rt(\指令解读_1_rt ), .rs_base(\指令解读_1_rs_base ));  // open: Func, OpCode
  Multiplexer #(.width(5), .enable("false")) multiplexer_1 (
    .in0(\指令解读_1_rd ), .in1(\指令解读_1_rt ), .out(out_5), .sel(controller_1_grf_op1));
  Multiplexer #(.select(2), .width(32), .enable("false")) multiplexer_2 (
    .in0(out_8), .in1(dm_1_memdata_2), .in2({im_of, {16{1'b0}}}), .out(RegDaata), .sel(controller_1_grf_op2));  // open: in3
  grf grf_1 (
    .clk(clk), .reset(reset), .WE(out_4), .WD(RegDaata), .A3(out_5), .RD1(grf_1_rd1), .RD2(out_9),
    .A1(\指令解读_1_rs_base ), .A2(\指令解读_1_rt ));
  assign bit_extender_1_out = {{16{1'b0}}, im_of};  // Bit_Extender bit_extender_1
  assign bit_extender_2_out = {{16{im_of[15]}}, im_of};  // Bit_Extender bit_extender_2
  Multiplexer #(.select(2), .width(32), .enable("false")) multiplexer_3 (
    .in0(out_9), .in1(bit_extender_1_out), .in2(bit_extender_2_out), .out(multiplexer_3_out),
    .sel(controller_1_alu_op));  // open: in3
  // Probe on grf_1_rd1
  ALU alu_1 (.a(grf_1_rd1), .op(controller_1_op), .b(multiplexer_3_out), .out(out_8));
  DM dm_1 (.MemAddr(out_8), .MemData(out_9), .MemWrite(out_7), .clk(clk), .rst(reset), .MemData_2(dm_1_memdata_2));
  // Probe on RegDaata
  // Probe on out_9
  // Probe on Instr
  // Probe on pc
  // Probe on out_5

  // Other names for the same wires on the sheet: MemAddr[31:0] = out_8; MemData[31:0] = out_9; MemWrite = out_7;
  //   RegAddr[4:0] = out_5; RegData[31:0] = RegDaata; RegWrite = out_4; rst = reset
endmodule

module IFU (
  input  [15:0] ctrl_addr,
  input  clk,
  input  rst,
  input  ctrl,
  output [31:0] PC,
  output [31:0] Instr
);

  wire [11:0] bit_extender_2_out;
  wire [31:0] adder_1_out, adder_2_out, bit_extender_1_out, multiplexer_1_out, PC_q, shifter_1_out;

  assign bit_extender_1_out = {{16{ctrl_addr[15]}}, ctrl_addr};  // Bit_Extender bit_extender_1
  Multiplexer #(.width(32), .enable("false")) multiplexer_1 (
    .in0(PC_q), .in1(adder_1_out), .out(multiplexer_1_out), .sel(ctrl));
  Adder #(.width(32)) adder_1 (.a(bit_extender_1_out), .b(PC_q), .out(adder_1_out));  // open: cin, cout
  Register #(.width(32)) u_PC (.D(adder_2_out), .Q(PC_q), .clk(clk), .clr(rst));  // open: en
  Adder #(.width(32)) adder_2 (.a(multiplexer_1_out), .b(32'h1), .out(adder_2_out));  // open: cin, cout
  Shifter #(.width(32)) shifter_1 (.in(PC_q), .\dist (5'b00010), .out(shifter_1_out));
  Bit_Extender #(.in_width(32), .out_width(12)) bit_extender_2 (.in(PC_q), .out(bit_extender_2_out));
  // Probe on bit_extender_2_out
  Adder #(.width(32)) adder_3 (.a(shifter_1_out), .b(32'h3000), .out(PC));  // open: cin, cout
  ROM #(.addrWidth(12), .dataWidth(32)) rom_1 (.addr(bit_extender_2_out), .data(Instr));  // open: sel
  // Probe on PC

  // Notes on the sheet:
  //   contents of rom_1 (hex, n*v repeats v):
  //   34000000 34020002 34030003 34040004 34050005 34060006 34070007 34080008 34090009 340a000a 340b000b
  //   340c000c 340d000d 340e000e 340f000f 34100010 34110011 34120012 34130013 34140014 34150015 34160016
  //   34170017 34180018 34190019 341a001a 341b001b 341c001c 341d001d 341e001e 341f001f 34000001 3402ffff
  //   34030000 3404000c 3c05ffff 3c060000 3c070008 a24020 3c097fff 1224820 1285020 1095022 a5020 445822
  //   826022 16c6820 a57022 ac4a0000 ac0b2ffc ac8cfffc 8cef0000 8c103000 8c112ffc
endmodule

// GRF
module grf (
  input  clk,
  input  reset,
  input  WE,
  input  [31:0] WD,
  input  [4:0] A1,
  input  [4:0] A2,
  input  [4:0] A3,
  output [31:0] RD1,
  output [31:0] RD2
);

  wire in0, in1, in2, in3, in4, in5, in6, in7, in8, in9, in10, in11, in12, in13, in14, in15, in16, in17,
       in18, in19, in20, in21, in22, in23, in24, in25, in26, in27, in28, in29, in30, in31;
  wire [31:0] out0, out1, out2, out3, out4, out5, out6, out7, out8, out9, out10, out11, out12, out13, out14,
       out15, out16, out17, out18, out19, out20, out21, out22, out23, out24, out25, out26, out27, out28,
       out29, out30, out31;

  Demultiplexer #(.select(5), .enable("false")) demultiplexer_1 (
    .out0(in0), .out1(in1), .out2(in2), .out3(in3), .out4(in4), .out5(in5), .out6(in6), .out7(in7),
    .out8(in8), .out9(in9), .out10(in10), .out11(in11), .out12(in12), .out13(in13), .out14(in14),
    .out15(in15), .out16(in16), .out17(in17), .out18(in18), .out19(in19), .out20(in20), .out21(in21),
    .out22(in22), .out23(in23), .out24(in24), .out25(in25), .out26(in26), .out27(in27), .out28(in28),
    .out29(in29), .out30(in30), .out31(in31), .in(WE), .sel(A3));
  Register #(.width(32)) register_1 (.D(WD), .en(in0), .Q(out0), .clk(clk), .clr(1'b1));
  Register #(.width(32)) register_2 (.D(WD), .en(in4), .Q(out4), .clk(clk), .clr(reset));
  Register #(.width(32)) register_3 (.D(WD), .en(in8), .Q(out8), .clk(clk), .clr(reset));
  Register #(.width(32)) register_4 (.D(WD), .en(in12), .Q(out12), .clk(clk), .clr(reset));
  Register #(.width(32)) register_5 (.D(WD), .en(in16), .Q(out16), .clk(clk), .clr(reset));
  Register #(.width(32)) register_6 (.D(WD), .en(in20), .Q(out20), .clk(clk), .clr(reset));
  Register #(.width(32)) register_7 (.D(WD), .en(in24), .Q(out24), .clk(clk), .clr(reset));
  Register #(.width(32)) register_8 (.D(WD), .en(in28), .Q(out28), .clk(clk), .clr(reset));
  Multiplexer #(.select(5), .width(32), .enable("false")) multiplexer_1 (
    .in0(out0), .in1(out1), .in2(out2), .in3(out3), .in4(out4), .in5(out5), .in6(out6), .in7(out7),
    .in8(out8), .in9(out9), .in10(out10), .in11(out11), .in12(out12), .in13(out13), .in14(out14),
    .in15(out15), .in16(out16), .in17(out17), .in18(out18), .in19(out19), .in20(out20), .in21(out21),
    .in22(out22), .in23(out23), .in24(out24), .in25(out25), .in26(out26), .in27(out27), .in28(out28),
    .in29(out29), .in30(out30), .in31(out31), .out(RD1), .sel(A1));
  Register #(.width(32)) register_9 (.D(WD), .en(in1), .Q(out1), .clk(clk), .clr(reset));
  Register #(.width(32)) register_10 (.D(WD), .en(in5), .Q(out5), .clk(clk), .clr(reset));
  Register #(.width(32)) register_11 (.D(WD), .en(in9), .Q(out9), .clk(clk), .clr(reset));
  Register #(.width(32)) register_12 (.D(WD), .en(in13), .Q(out13), .clk(clk), .clr(reset));
  Register #(.width(32)) register_13 (.D(WD), .en(in17), .Q(out17), .clk(clk), .clr(reset));
  Register #(.width(32)) register_14 (.D(WD), .en(in21), .Q(out21), .clk(clk), .clr(reset));
  Register #(.width(32)) register_15 (.D(WD), .en(in25), .Q(out25), .clk(clk), .clr(reset));
  Register #(.width(32)) register_16 (.D(WD), .en(in29), .Q(out29), .clk(clk), .clr(reset));
  Register #(.width(32)) register_17 (.D(WD), .en(in2), .Q(out2), .clk(clk), .clr(reset));
  Register #(.width(32)) register_18 (.D(WD), .en(in6), .Q(out6), .clk(clk), .clr(reset));
  Register #(.width(32)) register_19 (.D(WD), .en(in10), .Q(out10), .clk(clk), .clr(reset));
  Register #(.width(32)) register_20 (.D(WD), .en(in14), .Q(out14), .clk(clk), .clr(reset));
  Register #(.width(32)) register_21 (.D(WD), .en(in18), .Q(out18), .clk(clk), .clr(reset));
  Register #(.width(32)) register_22 (.D(WD), .en(in22), .Q(out22), .clk(clk), .clr(reset));
  Register #(.width(32)) register_23 (.D(WD), .en(in26), .Q(out26), .clk(clk), .clr(reset));
  Register #(.width(32)) register_24 (.D(WD), .en(in30), .Q(out30), .clk(clk), .clr(reset));
  Multiplexer #(.select(5), .width(32), .enable("false")) multiplexer_2 (
    .in0(out0), .in1(out1), .in2(out2), .in3(out3), .in4(out4), .in5(out5), .in6(out6), .in7(out7),
    .in8(out8), .in9(out9), .in10(out10), .in11(out11), .in12(out12), .in13(out13), .in14(out14),
    .in15(out15), .in16(out16), .in17(out17), .in18(out18), .in19(out19), .in20(out20), .in21(out21),
    .in22(out22), .in23(out23), .in24(out24), .in25(out25), .in26(out26), .in27(out27), .in28(out28),
    .in29(out29), .in30(out30), .in31(out31), .out(RD2), .sel(A2));
  Register #(.width(32)) register_25 (.D(WD), .en(in3), .Q(out3), .clk(clk), .clr(reset));
  Register #(.width(32)) register_26 (.D(WD), .en(in7), .Q(out7), .clk(clk), .clr(reset));
  Register #(.width(32)) register_27 (.D(WD), .en(in11), .Q(out11), .clk(clk), .clr(reset));
  Register #(.width(32)) register_28 (.D(WD), .en(in15), .Q(out15), .clk(clk), .clr(reset));
  Register #(.width(32)) register_29 (.D(WD), .en(in19), .Q(out19), .clk(clk), .clr(reset));
  Register #(.width(32)) register_30 (.D(WD), .en(in23), .Q(out23), .clk(clk), .clr(reset));
  Register #(.width(32)) register_31 (.D(WD), .en(in27), .Q(out27), .clk(clk), .clr(reset));
  Register #(.width(32)) register_32 (.D(WD), .en(in31), .Q(out31), .clk(clk), .clr(reset));
endmodule

module ALU (
  input  [31:0] a,
  input  [1:0] op,
  input  [31:0] b,
  output [31:0] out
);

  wire comparator_1_eq, comparator_1_lt;
  wire [31:0] adder_1_out, multiplexer_1_out, multiplexer_2_out, or_1_out, subtractor_1_out;

  Adder #(.width(32)) adder_1 (.a(a), .b(b), .out(adder_1_out));  // open: cin, cout
  Subtractor #(.width(32)) subtractor_1 (.a(a), .b(b), .out(subtractor_1_out));  // open: bin, bout
  assign or_1_out = a | b;  // OR_Gate or_1, 32 bits wide
  Comparator #(.width(32)) comparator_1 (.a(a), .b(b), .eq(comparator_1_eq), .lt(comparator_1_lt));  // open: gt
  Multiplexer #(.width(32), .enable("false")) multiplexer_1 (
    .in0(32'h1), .in1({32{1'b1}}), .out(multiplexer_1_out), .sel(comparator_1_lt));
  Multiplexer #(.width(32), .enable("false")) multiplexer_2 (
    .in0(multiplexer_1_out), .in1({32{1'b0}}), .out(multiplexer_2_out), .sel(comparator_1_eq));
  Multiplexer #(.select(2), .width(32), .enable("false")) multiplexer_3 (
    .in0(adder_1_out), .in1(subtractor_1_out), .in2(or_1_out), .in3(multiplexer_2_out), .out(out), .sel(op));
endmodule

module DM (
  input  [31:0] MemAddr,
  input  [31:0] MemData,
  input  MemWrite,
  input  clk,
  input  rst,
  output [31:0] MemData_2
);

  wire [10:0] bit_extender_1_out;
  wire [31:0] shifter_1_out;

  Shifter #(.width(32), .shift("lr")) shifter_1 (.in(MemAddr), .\dist (5'b00010), .out(shifter_1_out));
  Bit_Extender #(.in_width(32), .out_width(11)) bit_extender_1 (.in(shifter_1_out), .out(bit_extender_1_out));
  RAM #(.addrWidth(11), .dataWidth(32), .bus("separate")) ram_1 (
    .addr(bit_extender_1_out), .din(MemData), .data(MemData_2), .str(MemWrite), .clk(clk), .clr(rst));  // open: sel, ld
endmodule

// Con
module Controller (
  input  [31:0] Instr,
  input  [31:0] ALUout,
  output ctrl,
  output WE,
  output GRF_op1,
  output [1:0] GRF_op2,
  output [1:0] op,
  output [1:0] ALU_op,
  output MemWrite
);

  wire not_1_out, not_2_out, not_3_out, not_4_out, not_5_out, not_6_out, not_7_out, not_8_out, or_1_out,
       or_2_out, \与门阵列_1_add , \与门阵列_1_beq , \与门阵列_1_lui , \与门阵列_1_lw , \与门阵列_1_ori , \与门阵列_1_sub ;
  wire [1:0] multiplexer_1_out, multiplexer_3_out, multiplexer_4_out, multiplexer_5_out;
  wire [5:0] \指令解读_1_func , \指令解读_1_opcode ;

  \指令解读  \u_指令解读_1  (.Instr(Instr), .Func(\指令解读_1_func ), .OpCode(\指令解读_1_opcode ));  // open: im_of, rd, rt, rs_base
  not not_1 (not_1_out, \与门阵列_1_add );
  not not_2 (not_2_out, \与门阵列_1_sub );
  \与门阵列  \u_与门阵列_1  (
    .add(\与门阵列_1_add ), .sub(\与门阵列_1_sub ), .ori(\与门阵列_1_ori ), .lw(\与门阵列_1_lw ), .sw(MemWrite),
    .beq(\与门阵列_1_beq ), .lui(\与门阵列_1_lui ), .OpCode(\指令解读_1_opcode ), .Func(\指令解读_1_func ));
  not not_3 (not_3_out, \与门阵列_1_lw );
  not not_4 (not_4_out, \与门阵列_1_ori );
  not not_5 (not_5_out, MemWrite);
  not not_6 (not_6_out, \与门阵列_1_beq );
  not not_7 (not_7_out, \与门阵列_1_lui );
  or or_1 (or_1_out, \与门阵列_1_lw , MemWrite);
  or or_2 (or_2_out, \与门阵列_1_ori , \与门阵列_1_lui );
  and and_1 (ctrl, \与门阵列_1_beq , not_8_out);
  not not_8 (not_8_out, ALUout[0]);
  or or_3 (WE, \与门阵列_1_add , \与门阵列_1_sub , \与门阵列_1_ori , \与门阵列_1_lw , \与门阵列_1_lui );
  or or_4 (GRF_op1, \与门阵列_1_ori , \与门阵列_1_lw , \与门阵列_1_lui );
  Multiplexer #(.width(2), .enable("false")) multiplexer_1 (
    .in0(2'b00), .in1(2'b01), .out(multiplexer_1_out), .sel(\与门阵列_1_lw ));
  Multiplexer #(.width(2), .enable("false")) multiplexer_2 (
    .in0(multiplexer_1_out), .in1(2'b10), .out(GRF_op2), .sel(\与门阵列_1_lui ));
  Multiplexer #(.width(2), .enable("false")) multiplexer_3 (
    .in0(2'b00), .in1(2'b01), .out(multiplexer_3_out), .sel(\与门阵列_1_sub ));
  Multiplexer #(.width(2), .enable("false")) multiplexer_4 (
    .in0(multiplexer_3_out), .in1(2'b10), .out(multiplexer_4_out), .sel(\与门阵列_1_ori ));
  Multiplexer #(.width(2), .enable("false")) multiplexer_5 (
    .in0(2'b00), .in1(2'b10), .out(multiplexer_5_out), .sel(or_1_out));
  Multiplexer #(.width(2), .enable("false")) multiplexer_6 (
    .in0(multiplexer_4_out), .in1(2'b11), .out(op), .sel(\与门阵列_1_beq ));
  Multiplexer #(.width(2), .enable("false")) multiplexer_7 (
    .in0(multiplexer_5_out), .in1(2'b01), .out(ALU_op), .sel(or_2_out));
endmodule

// decode
module \指令解读  (
  input  [31:0] Instr,
  output [15:0] im_of,
  output [5:0] Func,
  output [4:0] rd,
  output [4:0] rt,
  output [4:0] rs_base,
  output [5:0] OpCode
);


  assign Func = Instr[5:0];
  assign im_of = Instr[15:0];
  assign OpCode = Instr[31:26];
  assign rd = Instr[15:11];
  assign rs_base = Instr[25:21];
  assign rt = Instr[20:16];
endmodule

module \暂存  (
  input  reset
);

  wire clk, controller_1_ctrl, controller_1_grf_op1, MemWrite, RegWrite, undriven;
  wire [1:0] ALU_op, GRF_op2, op;
  wire [4:0] RegAddr, \指令解读_1_rd , \指令解读_1_rs_base , \指令解读_1_rt ;
  wire [15:0] im_of;
  wire [31:0] bit_extender_1_out, bit_extender_2_out, DMout, grf_1_rd1, Instr, MemAddr, MemData,
       multiplexer_3_out, pc, RegData;

  Clock clock_1 (.out(clk));
  \指令解读  \u_指令解读_1  (
    .Instr(Instr), .im_of(im_of), .rd(\指令解读_1_rd ), .rt(\指令解读_1_rt ), .rs_base(\指令解读_1_rs_base ));  // open: Func, OpCode
  Controller controller_1 (
    .Instr(Instr), .ctrl(controller_1_ctrl), .WE(RegWrite), .GRF_op1(controller_1_grf_op1),
    .GRF_op2(GRF_op2), .op(op), .ALU_op(ALU_op), .MemWrite(MemWrite));  // open: ALUout
  IFU ifu_1 (.ctrl_addr(im_of), .clk(clk), .rst(reset), .ctrl(undriven), .PC(pc), .Instr(Instr));
  Multiplexer #(.width(5), .enable("false")) multiplexer_1 (
    .in0(\指令解读_1_rd ), .in1(\指令解读_1_rt ), .out(RegAddr), .sel(controller_1_grf_op1));
  Multiplexer #(.select(2), .width(32), .enable("false")) multiplexer_2 (
    .in0(MemAddr), .in1(DMout), .in2({im_of, {16{1'b0}}}), .out(RegData), .sel(GRF_op2));  // open: in3
  grf grf_1 (
    .clk(clk), .reset(reset), .WE(RegWrite), .WD(RegData), .A3(RegAddr), .RD1(grf_1_rd1), .RD2(MemData),
    .A1(\指令解读_1_rs_base ), .A2(\指令解读_1_rt ));
  assign bit_extender_1_out = {{16{1'b0}}, im_of};  // Bit_Extender bit_extender_1
  assign bit_extender_2_out = {{16{im_of[15]}}, im_of};  // Bit_Extender bit_extender_2
  DM dm_1 (.MemAddr(MemAddr), .MemData(MemData), .MemWrite(MemWrite), .clk(clk), .rst(reset), .MemData_2(DMout));
  ALU alu_1 (.a(grf_1_rd1), .op(op), .b(multiplexer_3_out), .out(MemAddr));
  Multiplexer #(.select(2), .width(32), .enable("false")) multiplexer_3 (
    .in0(MemData), .in1(bit_extender_1_out), .in2(bit_extender_2_out), .out(multiplexer_3_out), .sel(ALU_op));  // open: in3

  // Other names for the same wires on the sheet: out[31:0] = MemAddr; rst = reset
endmodule

module \与门阵列  (
  input  [5:0] OpCode,
  input  [5:0] Func,
  output add,
  output sub,
  output ori,
  output lw,
  output sw,
  output beq,
  output lui
);

  wire and_1_out, and_10_out, and_11_out, not_1_out, not_2_out, not_3_out, not_4_out, not_5_out, not_6_out,
       not_7_out, not_8_out, not_9_out, not_10_out, not_11_out, not_12_out;

  not not_1 (not_1_out, OpCode[5]);
  not not_2 (not_2_out, OpCode[4]);
  not not_3 (not_3_out, OpCode[3]);
  not not_4 (not_4_out, OpCode[1]);
  not not_5 (not_5_out, OpCode[2]);
  not not_6 (not_6_out, OpCode[0]);
  and and_1 (and_1_out, not_1_out, not_2_out, not_3_out, not_5_out, not_4_out, not_6_out);
  // AND_Gate and_2 has open pins: in0=not_1_out, in1=not_2_out, in2=OpCode[3], in3=OpCode[2], in4=not_4_out, in5=OpCode[0], out=open
  and and_3 (ori, not_1_out, not_2_out, OpCode[3], OpCode[2], not_4_out, OpCode[0]);
  and and_4 (lw, OpCode[5], not_2_out, not_3_out, not_5_out, OpCode[1], OpCode[0]);
  and and_5 (sw, OpCode[5], not_2_out, OpCode[3], not_5_out, OpCode[1], OpCode[0]);
  and and_6 (beq, not_1_out, not_2_out, not_3_out, OpCode[2], not_4_out, not_6_out);
  and and_7 (lui, not_1_out, not_2_out, OpCode[3], OpCode[2], OpCode[1], OpCode[0]);
  and and_8 (add, and_1_out, and_10_out);
  and and_9 (sub, and_1_out, and_11_out);
  and and_10 (and_10_out, Func[5], not_9_out, not_8_out, not_11_out, not_10_out, not_12_out);
  and and_11 (and_11_out, Func[5], not_9_out, not_8_out, not_11_out, Func[1], not_12_out);
  not not_7 (not_7_out, Func[5]);
  not not_8 (not_8_out, Func[3]);
  not not_9 (not_9_out, Func[4]);
  not not_10 (not_10_out, Func[1]);
  not not_11 (not_11_out, Func[2]);
  not not_12 (not_12_out, Func[0]);
endmodule

module IFU2 (
  input  [15:0] ctrl_addr,
  input  clk,
  input  rst,
  input  ctrl,
  output [31:0] PC,
  output [31:0] Instr
);

  wire [11:0] adder_1_out, adder_2_out, bit_extender_1_out, multiplexer_1_out, register_1_q;
  wire [31:0] bit_extender_2_out, shifter_1_out;

  Bit_Extender #(.in_width(16), .out_width(12)) bit_extender_1 (.in(ctrl_addr), .out(bit_extender_1_out));
  Multiplexer #(.width(12), .enable("false")) multiplexer_1 (
    .in0(register_1_q), .in1(adder_1_out), .out(multiplexer_1_out), .sel(ctrl));
  Adder #(.width(12)) adder_1 (.a(bit_extender_1_out), .b(register_1_q), .out(adder_1_out));  // open: cin, cout
  // Probe on nothing
  Adder #(.width(12)) adder_2 (.a(multiplexer_1_out), .b(12'h1), .out(adder_2_out));  // open: cin, cout
  Register #(.width(12)) register_1 (.D(adder_2_out), .Q(register_1_q), .clk(clk), .clr(rst));  // open: en
  assign bit_extender_2_out = {{20{1'b0}}, register_1_q};  // Bit_Extender bit_extender_2
  Shifter #(.width(32)) shifter_1 (.in(bit_extender_2_out), .\dist (5'b00010), .out(shifter_1_out));
  // Probe on register_1_q
  Adder #(.width(32)) adder_3 (.a(shifter_1_out), .b(32'h3000), .out(PC));  // open: cin, cout
  ROM #(.addrWidth(12), .dataWidth(32)) rom_1 (.addr(register_1_q), .data(Instr));  // open: sel
  // Probe on PC

  // Notes on the sheet:
  //   contents of rom_1 (hex, n*v repeats v):
  //   341c0000 341d0000 34013456 210820 8c010004 ac010004 3c027878 411822 3c051234 34040005 0 ac85ffff
  //   8c83ffff 10650001 1000000d 34670404 10e3000b 0 3c087777 3508ffff 80022 34001100 e65020 34080000
  //   34090001 340a0001 10a4020 1109fffe 1000ffff
endmodule

module \测试用  (
  output halt
);

  wire [31:0] PC;

  Comparator #(.width(32), .mode("unsigned")) comparator_1 (.a(PC), .b(32'h100), .gt(halt));  // open: eq, lt
endmodule
